# Fritzing sketch nano-button-led (saved by Fritzing 0.9.3b)
breadboards: 1

parts:
  Part1 = Arduino Nano (Rev3.0) (ICSP)
  R1 = Resistor [tolerance=±5% resistance=10k package=THT]
  R2 = Resistor [tolerance=±5% resistance=220 package=THT]
  LED1 = LED - 5mm [color="Red (633nm)" package="5 mm [THT]"]
  S2 = Pushbutton [package="[THT]"]

nets:
  N1: Part1.GND, R1.Pin_1, LED1.cathode
  N2: Part1.D5, R1.Pin_0, S2.Pin_1, S2.Pin_2
  N3: Part1.D6, R2.Pin_1
  N4: Part1.5V, S2.Pin_3, S2.Pin_4
  N5: R2.Pin_0, LED1.anode
